// Logisim project 6502logisimV37-New but no WozMon.circ as structural Verilog: 7 circuits, main circuit main
module main (
  input  in_1,
  input  IRQ,
  input  [7:0] in_3,
  input  in_4,
  input  in_5,
  input  in_6,
  input  in_7,
  input  in_8,
  input  in_9,
  input  in_10,
  input  PHI2,
  input  RDY,
  input  in_13,
  input  in_14,
  input  in_15,
  input  in_16,
  input  in_17,
  input  in_18,
  input  in_19,
  input  in_20,
  input  in_21,
  input  in_22,
  input  in_23,
  input  in_24,
  input  in_25,
  input  in_26,
  input  in_27,
  input  in_28,
  input  in_29,
  input  in_30,
  input  in_31,
  input  in_32,
  input  in_33,
  input  in_34,
  input  in_35,
  input  in_36,
  input  in_37,
  input  in_38,
  input  in_39,
  input  in_40,
  input  in_41,
  input  FS0,
  input  FS1,
  input  SETF,
  input  CLRF,
  input  in_46,
  input  in_47,
  input  in_48,
  input  in_49,
  input  in_50,
  input  in_51,
  input  in_52,
  input  in_53,
  input  in_54,
  input  in_55,
  input  in_56,
  input  in_57,
  input  in_58,
  input  in_59,
  input  in_60,
  input  in_61,
  input  in_62,
  input  MANUAL_CONTROL,
  output [7:0] out_64,
  output [7:0] PCH,
  output [7:0] PCL,
  output [7:0] out_67,
  output [7:0] out_68,
  output [7:0] out_69,
  output [7:0] out_70,
  output [7:0] out_71,
  output [7:0] out_72,
  output [7:0] out_73,
  output [7:0] out_74,
  output [7:0] ALU,
  output [3:0] out_76,
  output [7:0] out_77,
  output [7:0] out_78,
  output [7:0] FLG,
  output [7:0] out_80
);

  wire _CLK, _PCHW, _PCLW, AAW, ABW, ADHE, ADHR, ADHW, ADLR, ADLW, ALR, and_2_out, and_4_out, and_5_out,
       and_7_out, and_8_out, and_9_out, and_10_out, and_11_out, and_12_out, and_13_out, and_14_out,
       and_15_out, and_16_out, and_17_out, CG0, CG1, CG2, CLK, CLKAUX, d_ff_2_q, d_ff_3_qn, dip_74139_1_p4,
       dip_74139_1_p5, dip_74139_1_p6, EXTR, EXTW, FGS, FGV, FLAG, HCE, INT_DIS, INT_INS, IRW, L_EXTR,
       L_EXTW, LTCH_FLAG, NMI_INS, NMIR, nor_1_out, nor_2_out, nor_3_out, nor_4_out, nor_5_out, nor_6_out,
       nor_7_out, nor_8_out, not_1_out, not_5_out, not_6_out, not_7_out, not_8_out, not_9_out, not_10_out,
       not_12_out, not_13_out, not_14_out, not_15_out, not_16_out, not_17_out, not_18_out, not_19_out,
       not_20_out, not_21_out, not_22_out, not_24_out, not_25_out, not_26_out, not_27_out, not_28_out,
       not_29_out, not_30_out, not_31_out, not_32_out, not_33_out, not_34_out, not_35_out, not_36_out,
       not_37_out, not_38_out, not_39_out, not_40_out, not_41_out, not_42_out, not_43_out, not_44_out,
       not_45_out, or_1_out, or_2_out, or_4_out, or_5_out, or_6_out, or_7_out, or_8_out, pc_2_c_out, PCCE,
       PCHR, PCHRA, PCLR, PCSET, RAR, RAW, register_1_q, RST_INS, RXR, RXW, RYR, RYW, SPR, SPW, SRR, SRW,
       status_reg_1_carry, T0, T1, T2, t_ff_1_q, TCRST;
  wire [3:0] dip_74139_1_p2, dip_74161_2_p9, n8_bit_alu_1_c_out;
  wire [4:0] FG_SELECT;
  wire [7:0] controlled_buffer_18_out;
  wire [15:0] CTRL_1;
  wire [15:12] controlled_buffer_1_out;
  wire [31:0] CTRL_0;

  T_Flip_Flop t_ff_1 (
    .clk(1'b0), .T(1'b0), .Q(t_ff_1_q), .preset(in_7), .reset(dip_74139_1_p2[1]), .en(1'b1));  // open: Qn
  and and_1 (RST_INS, t_ff_1_q, T1);
  assign {controlled_buffer_1_out, NMIR, HCE, SRR, SRW, ALR, AAW, CG2, CG1, CG0, FGV, FGS, FG_SELECT[4]} = not_10_out ? CTRL_1 : 16'bz;  // Controlled_Buffer controlled_buffer_1
  not not_1 (not_1_out, IRQ);
  or or_1 (or_1_out, dip_74139_1_p2[2], dip_74139_1_p2[3]);
  not not_2 (T0, dip_74139_1_p4);
  not not_3 (T1, dip_74139_1_p5);
  not not_4 (T2, dip_74139_1_p6);
  ROM #(.addrWidth(13)) rom_1 (.addr({out_68, LTCH_FLAG, dip_74139_1_p2}), .data(CTRL_0[7:0]), .sel(1'b1));
  ROM #(.addrWidth(13)) rom_2 (.addr({out_68, LTCH_FLAG, dip_74139_1_p2}), .data(CTRL_0[15:8]), .sel(1'b1));
  ROM #(.addrWidth(13)) rom_3 (.addr({out_68, LTCH_FLAG, dip_74139_1_p2}), .data(CTRL_0[23:16]), .sel(1'b1));
  ROM #(.addrWidth(13)) rom_4 (.addr({out_68, LTCH_FLAG, dip_74139_1_p2}), .data(CTRL_0[31:24]), .sel(1'b1));
  ROM #(.addrWidth(13)) rom_5 (.addr({out_68, LTCH_FLAG, dip_74139_1_p2}), .data(CTRL_1[7:0]), .sel(1'b1));
  ROM #(.addrWidth(13)) rom_6 (.addr({out_68, LTCH_FLAG, dip_74139_1_p2}), .data(CTRL_1[15:8]), .sel(1'b1));
  Register #(.width(1)) register_1 (.D(status_reg_1_carry), .en(1'b1), .Q(register_1_q), .clk(_CLK), .clr(1'b0));
  assign {controlled_buffer_1_out, NMIR, HCE, SRR, SRW, ALR, AAW, CG2, CG1, CG0, FGV, FGS, FG_SELECT[4]} = MANUAL_CONTROL ? {in_61, in_60, in_59, in_58, in_57, in_56, in_55, in_54, in_53, in_52, in_51, in_50, in_49, in_48, in_47, in_46} : 16'bz;  // Controlled_Buffer controlled_buffer_2
  // DIP_74139 dip_74139_1: pin names not known; wires that end beside it: or_1_out, dip_74139_1_p2[0], dip_74139_1_p2[1], dip_74139_1_p4, dip_74139_1_p5, dip_74139_1_p6, 1'b0, 1'b0, 1'b0
  STATUS_REG status_reg_1 (
    .C(n8_bit_alu_1_c_out[0]), .Z(n8_bit_alu_1_c_out[1]), .V(n8_bit_alu_1_c_out[2]),
    .N(n8_bit_alu_1_c_out[3]), .C_C(FG_SELECT[0]), .C_Z(FG_SELECT[1]), .C_I(FG_SELECT[2]),
    .C_V(FG_SELECT[3]), .C_N(FG_SELECT[4]), .FGS(FGS), .FGV(FGV), .SRW(SRW), .BUS_IN(out_64), .CLK(CLK),
    .in_15(HCE), .CARRY(status_reg_1_carry), .I_DISABLE(INT_DIS), .FLAG(FLAG), .BUS_OUT(FLG));  // open: out_16
  not not_5 (not_5_out, INT_DIS);
  not not_6 (not_6_out, not_1_out);
  _8_BIT_ALU u_8_bit_alu_1 (
    .A_INPUT(out_73), .B_INPUT(out_77), .C_IN(register_1_q), .OP(out_76), .OUT(ALU),
    .C_OUT(n8_bit_alu_1_c_out[0]), .ZERO(n8_bit_alu_1_c_out[1]), .OVF(n8_bit_alu_1_c_out[2]),
    .NEG(n8_bit_alu_1_c_out[3]));
  and and_2 (and_2_out, not_5_out, not_6_out);
  not not_7 (not_7_out, IRW);
  or or_2 (or_2_out, TCRST, in_7);
  not not_8 (not_8_out, or_2_out);
  not not_9 (not_9_out, _CLK);
  assign {FG_SELECT[3:0], ADHE, PCHRA, EXTW, EXTR, TCRST, IRW, ADLW, ADLR, ADHW, ADHR, ABW, PCCE, _PCLW, PCLR, _PCHW, PCHR, SPW, SPR, RYW, RYR, RXW, RXR, out_76, RAW, RAR} = not_10_out ? CTRL_0 : 32'bz;  // Controlled_Buffer controlled_buffer_3
  not not_10 (not_10_out, MANUAL_CONTROL);
  and and_3 (INT_INS, and_2_out, T1);
  and and_4 (and_4_out, T2, CLK);
  not not_11 (_CLK, CLK);
  Register IR (.D(out_64), .en(not_7_out), .Q(out_68), .clk(CLK), .clr(1'b0));
  // DIP_74161 dip_74161_1: pin names not known; wires that end beside it: not_8_out, not_9_out, 1'b0, 1'b0, 1'b0, 1'b0, 1'b1, dip_74139_1_p2[0], dip_74139_1_p2[1], dip_74139_1_p2[2], dip_74139_1_p2[3], 1'b1, 1'b1
  Register register_2 (.D(out_64), .en(not_12_out), .Q(out_73), .clk(CLK), .clr(1'b0));
  not not_12 (not_12_out, AAW);
  Register register_3 (.D(out_64), .en(not_13_out), .Q(out_77), .clk(CLK), .clr(1'b0));
  not not_13 (not_13_out, ABW);
  assign out_64 = not_14_out ? FLG : 8'bz;  // Controlled_Buffer controlled_buffer_4
  not not_14 (not_14_out, SRR);
  D_Flip_Flop d_ff_1 (.clk(and_4_out), .D(FLAG), .Q(LTCH_FLAG), .en(1'b1));  // open: Qn, preset, reset
  Clock clock_1 (.out(CLK));
  CONSTANT_GENERATOR constant_generator_1 (
    .CG0(CG0), .CG1(CG1), .CG2(CG2), .RST_INS(RST_INS), .NMI_INS(NMI_INS), .HIGH(out_67), .LOW(out_64));
  assign {FG_SELECT[3:0], ADHE, PCHRA, EXTW, EXTR, TCRST, IRW, ADLW, ADLR, ADHW, ADHR, ABW, PCCE, _PCLW, PCLR, _PCHW, PCHR, SPW, SPR, RYW, RYR, RXW, RXR, out_76, RAW, RAR} = MANUAL_CONTROL ? {CLRF, SETF, FS1, FS0, in_41, in_40, in_39, in_38, in_37, in_36, in_35, in_34, in_33, in_32, in_31, in_30, in_29, in_28, in_27, in_26, in_25, in_24, in_23, in_22, in_21, in_20, in_19, in_18, in_17, in_16, in_15, in_14} : 32'bz;  // Controlled_Buffer controlled_buffer_5
  assign out_64 = not_15_out ? ALU : 8'bz;  // Controlled_Buffer controlled_buffer_6
  not not_15 (not_15_out, ALR);
  Pull_Resistor pull_resistor_1 (.node(out_64[5]));
  Pull_Resistor pull_resistor_2 (.node(out_64[7]));
  Pull_Resistor pull_resistor_3 (.node(out_64[6]));
  D_Flip_Flop d_ff_2 (.clk(in_1), .D(1'b1), .Q(d_ff_2_q), .en(1'b1), .reset(NMIR));  // open: Qn, preset
  not not_16 (not_16_out, SPW);
  not not_17 (not_17_out, RXW);
  not not_18 (not_18_out, RYW);
  not not_19 (not_19_out, RAW);
  not not_20 (not_20_out, ADHW);
  assign out_67 = not_20_out ? out_64 : 8'bz;  // Controlled_Buffer controlled_buffer_7
  Pull_Resistor pull_resistor_4 (.node(out_64[1]));
  Pull_Resistor pull_resistor_5 (.node(out_64[4]));
  Pull_Resistor pull_resistor_6 (.node(out_64[2]));
  Pull_Resistor pull_resistor_7 (.node(out_64[3]));
  and and_5 (and_5_out, _PCHW, PCSET);
  Register SP (.D(out_64), .en(not_16_out), .Q(out_69), .clk(CLK), .clr(1'b0));
  Register RX (.D(out_64), .en(not_17_out), .Q(out_70), .clk(CLK), .clr(1'b0));
  Register RY (.D(out_64), .en(not_18_out), .Q(out_71), .clk(CLK), .clr(1'b0));
  Register RA (.D(out_64), .en(not_19_out), .Q(out_74), .clk(CLK), .clr(1'b0));
  Register register_4 (.D(out_67), .en(not_21_out), .Q(out_78), .clk(CLK), .clr(1'b0));
  not not_21 (not_21_out, ADHE);
  Register register_5 (.D(out_64), .en(not_22_out), .Q(out_80), .clk(CLK), .clr(1'b0));
  not not_22 (not_22_out, ADLW);
  Pull_Resistor pull_resistor_8 (.node(out_64[0]));
  and and_6 (NMI_INS, d_ff_2_q, T1);
  assign out_64 = in_6 ? in_3 : 8'bz;  // Controlled_Buffer controlled_buffer_8
  not not_23 (PCSET, in_6);
  PC pc_1 (
    .DATA_IN(out_64), .CLK(CLKAUX), .CLEAR(1'b0), .LOAD(and_5_out), .COUNT(pc_2_c_out), .DATA_OUT(PCH));  // open: C_OUT
  PC pc_2 (
    .DATA_IN(out_64), .CLK(CLK), .CLEAR(1'b0), .LOAD(_PCLW), .COUNT(and_7_out), .C_OUT(pc_2_c_out),
    .DATA_OUT(PCL));
  assign out_64 = and_8_out ? PCL : 8'bz;  // Controlled_Buffer controlled_buffer_9
  assign out_64 = not_24_out ? out_69 : 8'bz;  // Controlled_Buffer controlled_buffer_10
  not not_24 (not_24_out, SPR);
  assign out_64 = not_25_out ? out_70 : 8'bz;  // Controlled_Buffer controlled_buffer_11
  not not_25 (not_25_out, RXR);
  assign out_64 = not_26_out ? out_71 : 8'bz;  // Controlled_Buffer controlled_buffer_12
  not not_26 (not_26_out, RYR);
  assign out_64 = not_27_out ? out_74 : 8'bz;  // Controlled_Buffer controlled_buffer_13
  not not_27 (not_27_out, RAR);
  assign out_64 = not_28_out ? out_78 : 8'bz;  // Controlled_Buffer controlled_buffer_14
  not not_28 (not_28_out, ADHR);
  assign out_64 = not_29_out ? out_80 : 8'bz;  // Controlled_Buffer controlled_buffer_15
  not not_29 (not_29_out, ADLR);
  assign out_64 = not_30_out ? PCH : 8'bz;  // Controlled_Buffer controlled_buffer_16
  not not_30 (not_30_out, PCHR);
  not not_31 (not_31_out, PCLR);
  and and_7 (and_7_out, PCCE, not_33_out);
  and and_8 (and_8_out, not_31_out, PCSET);
  assign out_67 = not_32_out ? PCH : 8'bz;  // Controlled_Buffer controlled_buffer_17
  not not_32 (not_32_out, PCHRA);
  not not_33 (not_33_out, INT_INS);
  or or_3 (CLKAUX, in_4, CLK);
  Pull_Resistor pull_resistor_9 (.node(out_67[7]));
  Pull_Resistor pull_resistor_10 (.node(out_67[6]));
  Pull_Resistor pull_resistor_11 (.node(out_67[5]));
  Pull_Resistor pull_resistor_12 (.node(out_67[4]));
  Pull_Resistor pull_resistor_13 (.node(out_67[2]));
  Pull_Resistor pull_resistor_14 (.node(out_67[0]));
  Pull_Resistor pull_resistor_15 (.node(out_67[1]));
  Pull_Resistor pull_resistor_16 (.node(out_67[3]));
  or or_4 (or_4_out, INT_INS, RST_INS);
  or or_5 (or_5_out, NMI_INS, or_4_out);
  and and_9 (and_9_out, _CLK, L_EXTR);
  and and_10 (and_10_out, _CLK, L_EXTW);
  not not_34 (not_34_out, PHI2);
  not not_35 (not_35_out, or_5_out);
  or or_6 (or_6_out, and_9_out, and_10_out);
  assign controlled_buffer_18_out = and_11_out ? out_64 : 8'bz;  // Controlled_Buffer controlled_buffer_18
  assign out_64 = and_12_out ? controlled_buffer_18_out : 8'bz;  // Controlled_Buffer controlled_buffer_19
  nor nor_1 (nor_1_out, in_8, nor_2_out);
  nor nor_2 (nor_2_out, nor_1_out, in_10);
  not not_36 (not_36_out, not_34_out);
  and and_11 (and_11_out, and_10_out, not_42_out);
  and and_12 (and_12_out, not_42_out, not_40_out);
  Pull_Resistor pull_resistor_17 (.node(nor_1_out));
  not not_37 (not_37_out, not_36_out);
  not not_38 (not_38_out, not_37_out);
  D_Flip_Flop d_ff_3 (.clk(not_34_out), .D(RDY), .Qn(d_ff_3_qn), .en(1'b1));  // open: Q, preset, reset
  D_Flip_Flop d_ff_4 (.clk(CLK), .D(EXTR), .Q(L_EXTR));  // open: Qn, preset, en, reset
  D_Flip_Flop d_ff_5 (.clk(CLK), .D(EXTW), .Q(L_EXTW));  // open: Qn, preset, en, reset
  not not_39 (not_39_out, and_13_out);
  and and_13 (and_13_out, not_35_out, or_6_out);
  not not_40 (not_40_out, and_10_out);
  not not_41 (not_41_out, L_EXTW);
  or or_7 (or_7_out, not_38_out, d_ff_3_qn);
  not not_42 (not_42_out, not_39_out);
  nor nor_3 (nor_3_out, in_9, in_9);
  not not_43 (not_43_out, or_7_out);
  nor nor_4 (nor_4_out, nor_3_out, nor_3_out);
  // DIP_74161 dip_74161_2: pin names not known; wires that end beside it: nor_2_out, 1'b1, not_43_out, 1'b0, 1'b0, 1'b0, 1'b0, 1'b1, dip_74161_2_p9[0], dip_74161_2_p9[1], dip_74161_2_p9[2], dip_74161_2_p9[3], 1'b1, 1'b1
  not not_44 (not_44_out, not_41_out);
  nor nor_5 (nor_5_out, nor_4_out, nor_4_out);
  or or_8 (or_8_out, not_44_out, not_41_out);
  nor nor_6 (nor_6_out, in_9, nor_5_out);
  and and_14 (and_14_out, 1'b1, or_8_out);
  nor nor_7 (nor_7_out, in_5, nor_8_out);
  nor nor_8 (nor_8_out, nor_7_out, nor_6_out);
  RAM #(.addrWidth(16), .bus("asynch")) ram_1 (
    .addr({out_78, out_80}), .data(out_72), .sel(and_14_out), .ld(not_45_out), .clr(in_13));
  not not_45 (not_45_out, and_16_out);
  and and_15 (and_15_out, and_14_out, not_44_out);
  and and_16 (and_16_out, not_44_out, _CLK);
  Pull_Resistor pull_resistor_18 (.node(nor_7_out));
  assign out_72 = and_15_out ? controlled_buffer_18_out : 8'bz;  // Controlled_Buffer controlled_buffer_20
  assign controlled_buffer_18_out = and_17_out ? out_72 : 8'bz;  // Controlled_Buffer controlled_buffer_21
  and and_17 (and_17_out, and_14_out, not_41_out);

  // Other names for the same wires on the sheet: ALUOP[3:0] = out_76; DBUS[7:0] = out_64; RESET = in_7

  // Notes on the sheet:
  //   ROM 2
  //   ROM 3
  //   ROM 4
  //   STATUS REGISTER
  //   RESET AND INTERRUPT LOGIC
  //   ROM 0
  //   ROM 1
  //   ROM 5
  //   contents of rom_1 (hex, n*v repeats v):
  //   4*c3 e3 c3 c3 e3 c3 c3 e3 9*c3 e3 c3 c3 e3 c3 c3 e3 9*c3 83 e7 c3 df c3 c2 c3 c3 c3 c2 c9 5*c3 83 e7
  //   c3 df c3 c2 c3 c3 c3 c2 c9 102*c3 c2 c9 14*c3 c2 c9 14*c3 d7 15*c3 d7 46*c3 e3 15*c3 e3 16*c3 c2 c9
  //   14*c3 c2 c9 11*c3 c2 d5 14*c3 c2 d5 84*c3 c2 c9 14*c3 c2 c9 14*c3 d7 15*c3 d7 44*c3 e7 ef c3 e7
  //   28*c3 df c3 c3 c3 e7 c3 df c3 c2 c9 6*c3 df c3 c3 c3 e7 c3 df c3 c2 c9 101*c3 83 e7 c3 c2 c9 11*c3
  //   83 e7 c3 c2 c9 11*c3 83 e7 c3 d7 12*c3 83 e7 c3 d7 79*c3 e7 c3 df c3 c2 c9 10*c3 e7 c3 df c3 c2 c9
  //   103*c3 83 c3 c3 e7 c3 df c3 c2 c9 7*c3 83 c3 c3 e7 c3 df c3 c2 c9 7*c3 83 c3 c3 e7 c3 df c3 d7 8*c3
  //   83 c3 c3 e7 c3 df c3 d7 42*c3 e3 c3 c3 c3 e3 c3 c3 c3 e7 7*c3 e3 c3 c3 c3 e3 c3 c3 c3 e7 5*c3 83 e7
  //   c3 df c3 c2 c3 c3 c3 c2 d1 5*c3 83 e7 c3 df c3 c2 c3 c3 c3 c2 d1 70*c3 c2 f3 14*c3 c2 f3 14*c3 c2 d1
  //   14*c3 c2 d1 14*c3 d7 15*c3 d7 45*c3 df 15*c3 df 17*c3 c2 d1 14*c3 c2 d1 11*c3 c2 d5 14*c3 c2 d5
  //   52*c3 c2 f3 14*c3 c2 f3 14*c3 c2 d1 14*c3 c2 d1 14*c3 d7 15*c3 d7 60*c3 e7 ef c3 e7 12*c3 df c3 c3
  //   c3 e7 c3 df c3 c2 d1 6*c3 df c3 c3 c3 e7 c3 df c3 c2 d1 101*c3 83 e7 c3 c2 d1 11*c3 83 e7 c3 c2 d1
  //   11*c3 83 e7 c3 d7 12*c3 83 e7 c3 d7 79*c3 e7 c3 df c3 c2 d1 10*c3 e7 c3 df c3 c2 d1 103*c3 83 c3 c3
  //   e7 c3 df c3 c2 d1 7*c3 83 c3 c3 e7 c3 df c3 c2 d1 7*c3 83 c3 c3 e7 c3 df c3 d7 8*c3 83 c3 c3 e7 c3
  //   df c3 d7 39*c3 df c3 c3 c3 df c3 c3 c3 df 7*c3 df c3 c3 c3 df c3 c3 c3 df 8*c3 83 e7 c3 df c3 c2 c3
  //   c3 c3 c2 cd 5*c3 83 e7 c3 df c3 c2 c3 c3 c3 c2 cd 102*c3 c2 cd 14*c3 c2 cd 14*c3 db 15*c3 db 45*c3
  //   c2 e3 14*c3 c2 e3 16*c3 c2 cd 14*c3 c2 cd 11*c3 c2 d9 14*c3 c2 d9 84*c3 c2 cd 14*c3 c2 cd 14*c3 db
  //   15*c3 db 44*c3 e7 ef c3 e7 28*c3 df c3 c3 c3 e7 c3 df c3 c2 cd 6*c3 df c3 c3 c3 e7 c3 df c3 c2 cd
  //   101*c3 83 e7 c3 c2 cd 11*c3 83 e7 c3 c2 cd 11*c3 83 e7 c3 db 12*c3 83 e7 c3 db 79*c3 e7 c3 df c3 c2
  //   cd 10*c3 e7 c3 df c3 c2 cd 103*c3 83 c3 c3 e7 c3 df c3 c2 cd 7*c3 83 c3 c3 e7 c3 df c3 c2 cd 7*c3 83
  //   c3 c3 e7 c3 df c3 db 8*c3 83 c3 c3 e7 c3 df c3 db 39*c3 df c3 c3 c3 df 11*c3 df c3 c3 c3 df 12*c3 83
  //   e7 c3 df c3 c2 c3 c3 c3 c2 e5 5*c3 83 e7 c3 df c3 c2 c3 c3 c3 c2 e5 102*c3 c2 e5 14*c3 c2 e5 14*c3
  //   db 15*c3 db 45*c3 df c3 c3 c1 12*c3 df c3 c3 c1 14*c3 c2 e5 14*c3 c2 e5 11*c3 c2 d9 14*c3 c2 d9
  //   53*c3 df c3 df 13*c3 df c3 df 12*c3 c2 e5 14*c3 c2 e5 14*c3 db 15*c3 db 60*c3 e7 ef c3 e7 12*c3 df
  //   c3 c3 c3 e7 c3 df c3 c2 e5 6*c3 df c3 c3 c3 e7 c3 df c3 c2 e5 101*c3 83 e7 c3 c2 e5 11*c3 83 e7 c3
  //   c2 e5 11*c3 83 e7 c3 db 12*c3 83 e7 c3 db 79*c3 e7 c3 df c3 c2 e5 10*c3 e7 c3 df c3 c2 e5 103*c3 83
  //   c3 c3 e7 c3 df c3 c2 e5 7*c3 83 c3 c3 e7 c3 df c3 c2 e5 7*c3 83 c3 c3 e7 c3 df c3 db 8*c3 83 c3 c3
  //   e7 c3 df c3 db 72*c3 83 e7 c3 df c3 c2 c3 c3 c2 7*c3 83 e7 c3 df c3 c2 c3 c3 c2 103*c3 c2 15*c3 c2
  //   15*c3 83 15*c3 83 46*c3 e3 15*c3 e3 46*c3 83 c1 14*c3 83 c1 83*c3 c2 15*c3 c2 15*c3 83 15*c3 83
  //   45*c3 e7 ef c3 e7 28*c3 df c3 c3 c3 e7 c3 df c2 8*c3 df c3 c3 c3 e7 c3 df c2 71*c3 83 e7 14*c3 83 e7
  //   14*c3 83 e7 c2 13*c3 83 e7 c2 14*c3 e7 83 14*c3 e7 83 44*c3 c1 15*c3 c1 19*c3 e7 c3 df c2 12*c3 e7
  //   c3 df c2 7*c3 83 15*c3 83 81*c3 83 c3 c3 e7 c3 df c2 9*c3 83 c3 c3 e7 c3 df c2 105*c3 83 e7 c3 df c3
  //   c2 c3 c3 c3 c1 6*c3 83 e7 c3 df c3 c2 c3 c3 c3 c1 7*c3 43 15*c3 43 79*c3 c1 15*c3 c1 15*c3 43 15*c3
  //   43 44*c3 c2 15*c3 c2 18*c3 c1 15*c3 c1 12*c3 c2 43 14*c3 c2 43 84*c3 c1 15*c3 c1 15*c3 43 15*c3 43
  //   60*c3 e7 ef c3 e7 12*c3 df c3 c3 c3 e7 c3 df c3 c1 7*c3 df c3 c3 c3 e7 c3 df c3 c1 70*c3 83 e7 14*c3
  //   83 e7 14*c3 83 e7 c3 c1 12*c3 83 e7 c3 c1 13*c3 e7 c3 43 13*c3 e7 c3 43 79*c3 e7 c3 df c3 c1 11*c3
  //   e7 c3 df c3 c1 7*c3 43 15*c3 43 48*c3 83 c3 c3 e7 c3 df 10*c3 83 c3 c3 e7 c3 df 10*c3 83 c3 c3 e7 c3
  //   df c3 c1 8*c3 83 c3 c3 e7 c3 df c3 c1 11*c3 e7 c3 df c3 43 11*c3 e7 c3 df c3 43 42*c3 eb 15*c3 eb
  //   13*c3 83 e7 c3 df c3 c2 c3 c3 c3 c2 eb 5*c3 83 e7 c3 df c3 c2 c3 c3 c3 c2 eb 71*c3 eb 15*c3 eb 14*c3
  //   c2 eb 14*c3 c2 eb 14*c3 e3 15*c3 e3 45*c3 df 15*c3 df 17*c3 c2 eb 14*c3 c2 eb 11*c3 83 63 14*c3 83
  //   63 53*c3 eb 15*c3 eb 14*c3 c2 eb 14*c3 c2 eb 14*c3 e3 15*c3 e3 44*c3 e7 ef c3 e7 28*c3 df c3 c3 c3
  //   e7 c3 df c3 c2 eb 6*c3 df c3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
  //   contents of rom_2 (hex, n*v repeats v):
  //   bf ff fb ef f7 fb bf f7 fb ff f7 ff 7f ff df ff bf ff fb ef f7 fb bf f7 fb ff f7 ff 7f ff df ff bf
  //   ff bf 13*ff bf ff bf 13*ff bf 15*ff bf 15*ff bf 15*ff bf 15*ff bf 15*ff bf 15*ff bf ff bf 13*ff bf
  //   ff bf 13*ff bf ff bf 13*ff bf ff bf 13*ff bf 15*ff bf 15*ff bf ff fb ff f7 11*ff bf ff fb ff f7
  //   11*ff bf ff bf 13*ff bf ff bf 13*ff bf 15*ff bf 15*ff bf 15*ff bf 15*ff bf 15*ff bf 15*ff bf ff bf
  //   ff bf 11*ff bf ff bf ff bf 11*ff bf ff bf ff bf 11*ff bf ff bf ff bf 11*ff bf 15*ff bf 15*ff bf ff
  //   bf ff bf 7f ff ef df 7*ff bf ff bf 13*ff bf ff bf 4*ff fe 8*ff bf ff bf 4*ff fe 8*ff bf 15*ff bf
  //   15*ff bf 15*ff bf 15*ff bf 15*ff bf 15*ff bf ff bf 13*ff bf ff bf 13*ff bf ff bf 13*ff bf ff bf
  //   13*ff bf 15*ff bf 15*ff bf 15*ff bf 15*ff bf ff bf ff fe bf 10*ff bf ff bf ff fe bf 10*ff bf 15*ff
  //   bf 15*ff bf 15*ff bf 15*ff bf 15*ff bf 15*ff bf ff bf ff ff bf 10*ff bf ff bf ff ff bf 10*ff bf ff
  //   bf ff ff bf 10*ff bf ff bf ff ff bf 10*ff bf 15*ff bf 15*ff bf ff bf ff fb ef f7 fb bf fb f7 bf df
  //   ff 7f ff bf ff bf ff fb ef f7 fb bf fb f7 bf df ff 7f ff bf ff bf 13*ff bf ff bf 13*ff bf 15*ff bf
  //   15*ff bf 15*ff bf 15*ff bf ff bf 13*ff bf ff bf 13*ff bf ff bf 13*ff bf ff bf 13*ff bf ff bf 13*ff
  //   bf ff bf 13*ff bf 15*ff bf 15*ff bf ff fb f7 fb 11*ff bf ff fb f7 fb 11*ff bf ff bf 13*ff bf ff bf
  //   13*ff bf 15*ff bf 15*ff bf 15*ff bf 15*ff bf ff bf ff bf 11*ff bf ff bf ff bf 11*ff bf ff bf ff bf
  //   11*ff bf ff bf ff bf 11*ff bf ff bf ff bf 11*ff bf ff bf ff bf 11*ff bf 15*ff bf 15*ff bf ff bf
  //   13*ff bf ff bf ff bf 7f ff ef df 7*ff bf ff bf 4*ff fe 8*ff bf ff bf 4*ff fe 8*ff bf 15*ff bf 15*ff
  //   bf 15*ff bf 15*ff bf 15*ff bf 15*ff bf ff bf 13*ff bf ff bf 13*ff bf ff bf 13*ff bf ff bf 13*ff bf
  //   15*ff bf 15*ff bf 15*ff bf 15*ff bf ff bf ff fe bf 10*ff bf ff bf ff fe bf 10*ff bf 15*ff bf 15*ff
  //   bf 15*ff bf 15*ff bf 15*ff bf 15*ff bf ff bf ff ff bf 10*ff bf ff bf ff ff bf 10*ff bf ff bf ff ff
  //   bf 10*ff bf ff bf ff ff bf 10*ff bf 15*ff bf 15*ff bf ff fb f7 fb ff fb f7 fb 7f fb f7 fb df ff ff
  //   bf ff fb f7 fb ff fb f7 fb 7f fb f7 fb df ff ff bf ff bf 13*ff bf ff bf 13*ff bf 15*ff bf 15*ff bf
  //   15*ff bf 15*ff bf 15*ff bf 15*ff bf ff bf 13*ff bf ff bf 13*ff bf ff bf 13*ff bf ff bf 13*ff bf
  //   15*ff bf 15*ff bf ff fb ff f7 11*ff bf ff fb ff f7 11*ff bf ff bf 13*ff bf ff bf 13*ff bf 15*ff bf
  //   15*ff bf 15*ff bf 15*ff bf ff bf ff bf df 7f 9*ff bf ff bf ff bf df 7f 9*ff bf ff bf ff bf 11*ff bf
  //   ff bf ff bf 11*ff bf ff bf ff bf 11*ff bf ff bf ff bf 11*ff bf 15*ff bf 15*ff bf ff bf ff bf 7f ff
  //   ef df 7*ff bf ff bf 13*ff bf ff bf 4*ff fe 8*ff bf ff bf 4*ff fe 8*ff bf 15*ff bf 15*ff bf 15*ff bf
  //   15*ff bf 15*ff bf 15*ff bf ff bf 13*ff bf ff bf 13*ff bf ff bf 13*ff bf ff bf 13*ff bf 15*ff bf
  //   15*ff bf 15*ff bf 15*ff bf ff bf ff fe bf 10*ff bf ff bf ff fe bf 10*ff bf 15*ff bf 15*ff bf 15*ff
  //   bf 15*ff bf 15*ff bf 15*ff bf ff bf ff ff bf 10*ff bf ff bf ff ff bf 10*ff bf ff bf ff ff bf 10*ff
  //   bf ff bf ff ff bf 10*ff bf 15*ff bf 15*ff bf ff fb f7 fb 7f fb f7 fb df 6*ff bf ff fb f7 fb 7f fb f7
  //   fb df 6*ff bf ff bf 13*ff bf ff bf 13*ff bf 15*ff bf 15*ff bf 15*ff bf 15*ff bf 15*ff bf 15*ff bf ff
  //   bf 13*ff bf ff bf 13*ff bf ff bf 13*ff bf ff bf 13*ff bf 15*ff bf 15*ff bf ff fb f7 fb 11*ff bf ff
  //   fb f7 fb 11*ff bf ff bf 13*ff bf ff bf 13*ff bf 15*ff bf 15*ff bf 15*ff bf 15*ff bf ff bf ff bf ff
  //   ff 7f 4*ff df ff ff ff bf ff bf ff bf ff ff 7f 4*ff df ff ff ff bf ff bf ff bf 11*ff bf ff bf ff bf
  //   11*ff bf ff bf ff bf 11*ff bf ff bf ff bf 11*ff bf 15*ff bf 15*ff bf ff bf 13*ff bf ff bf ff bf 7f
  //   ff ef df 7*ff bf ff bf 4*ff fe 8*ff bf ff bf 4*ff fe 8*ff bf 15*ff bf 15*ff bf 15*ff bf 15*ff bf
  //   15*ff bf 15*ff bf ff bf 13*ff bf ff bf 13*ff bf ff bf 13*ff bf ff bf 13*ff bf 15*ff bf 15*ff bf
  //   15*ff bf 15*ff bf ff bf ff fe bf 10*ff bf ff bf ff fe bf 10*ff bf 15*ff bf 15*ff bf 15*ff bf 15*ff
  //   bf 15*ff bf 15*ff bf ff bf ff ff bf 10*ff bf ff bf ff ff bf 10*ff bf ff bf ff ff bf 10*ff bf ff bf
  //   ff ff bf 10*ff bf 15*ff bf 15*ff bf 15*ff bf 15*ff bf ff bf 13*ff bf ff bf 13*ff bf 15*ff bf 15*ff
  //   bf 15*ff bf 15*ff bf ff bf ff fe 11*ff bf ff bf ff fe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
  //   contents of rom_3 (hex, n*v repeats v):
  //   5e 3f 5f 7e 7e 5e 7e 7e 5e 7e 7e 5e 7e 5e 7e fe 5e 3f 5f 7e 7e 5e 7e 7e 5e 7e 7e 5e 7e 5e 7e fe 5e
  //   3f 5e 7f 7c 5e 76 5e 7a 7c 76 5e 7e 7c 7e fe 5e 3f 5e 7f 7c 5e 76 5e 7a 7c 76 5e 7e 7c 7e fe 5e 3f
  //   fe 13*7e 5e 3f fe 13*7e 5e 3f fe 13*7e 5e 3f fe 13*7e 5e 3f fe 13*7e 5e 3f fe 13*7e 5e 3f 5e 5f 7e
  //   7c 7e fe 8*7e 5e 3f 5e 5f 7e 7c 7e fe 8*7e 5e 3f 5e 5f 7e 7e fe 9*7e 5e 3f 5e 5f 7e 7e fe 9*7e 5e 3f
  //   fe 13*7e 5e 3f fe 13*7e 5e 3f 5e 7e 7e fe 10*7e 5e 3f 5e 7e 7e fe 10*7e 5e 3f 5e 7f 7e 7c 7e fe 8*7e
  //   5e 3f 5e 7f 7e 7c 7e fe 8*7e 5e 3f 7e 7e fe 11*7e 5e 3f 7e 7e fe 11*7e 5e 3f fe 13*7e 5e 3f fe 13*7e
  //   5e 3f fe 13*7e 5e 3f fe 13*7e 5e 3f 5e 7f 5e 77 5e 7e 7c 7e fe 5*7e 5e 3f 5e 7f 5e 77 5e 7e 7c 7e fe
  //   5*7e 5e 3f 5e 7f 5e 77 5e 7e 7e fe 6*7e 5e 3f 5e 7f 5e 77 5e 7e 7e fe 6*7e 5e 3f fe 13*7e 5e 3f fe
  //   13*7e 5e 3f 5e 7f 7c 7e 7e 7c 7e fe 6*7e 5e 3f 5e 7f fe 11*7e 5e 3f 5e 5f 76 5e 7a 7c 76 5e 7a 76 7e
  //   7c 7e fe 5e 3f 5e 5f 76 5e 7a 7c 76 5e 7a 76 7e 7c 7e fe 5e 3f fe 13*7e 5e 3f fe 13*7e 5e 3f fe
  //   13*7e 5e 3f fe 13*7e 5e 3f fe 13*7e 5e 3f fe 13*7e 5e 3f 5e 7f 7c 5e 7e 7c 7e fe 6*7e 5e 3f 5e 7f 7c
  //   5e 7e 7c 7e fe 6*7e 5e 3f 5e 7f 7c 5e 7e 7e fe 7*7e 5e 3f 5e 7f 7c 5e 7e 7e fe 7*7e 5e 3f fe 13*7e
  //   5e 3f fe 13*7e 5e 3f 7e fe 12*7e 5e 3f 7e fe 12*7e 5e 3f 5e 7f 7c 5e 77 5e 7a 76 7e 7c 7e fe 7e 7e
  //   5e 3f 5e 7f 7c 5e 77 5e 7a 76 7e 7c 7e fe 7e 7e 5e 3f fe 13*7e 5e 3f fe 13*7e 5e 3f fe 13*7e 5e 3f
  //   fe 13*7e 5e 3f fe 13*7e 5e 3f fe 13*7e 5e 3f 5e 7f 7c 5e 77 5e 7a 76 7e 7c 7e fe 7e 7e 5e 3f 5e 7f
  //   7c 5e 77 5e 7a 76 7e 7c 7e fe 7e 7e 5e 3f 5e 7f 7c 5e 77 5e 7a 76 7e 7e fe 7e 7e 7e 5e 3f 5e 7f 7c
  //   5e 77 5e 7a 76 7e 7e fe 7e 7e 7e 5e 3f fe 13*7e 5e 3f fe 13*7e 5e 3f 5e 7c 5f 7e 7e 5e 7e 7e 7e 5e
  //   7e 7e 7e fe 5e 3f 5e 7c 5f 7e 7e 5e 7e 7e 7e 5e 7e 7e 7e fe 5e 3f 5e 7f 7c 5e 76 5e 7a 7c 76 5e 7e
  //   7c 7e fe 5e 3f 5e 7f 7c 5e 76 5e 7a 7c 76 5e 7e 7c 7e fe 5e 3f fe 13*7e 5e 3f fe 13*7e 5e 3f fe
  //   13*7e 5e 3f fe 13*7e 5e 3f 5e 5f 7e 7c 7e fe 8*7e 5e 3f 5e 5f 7e 7c 7e fe 8*7e 5e 3f 5e 5f 7e 7c 7e
  //   fe 8*7e 5e 3f 5e 5f 7e 7c 7e fe 8*7e 5e 3f 5e 5f 7e 7e fe 9*7e 5e 3f 5e 5f 7e 7e fe 9*7e 5e 3f fe
  //   13*7e 5e 3f fe 13*7e 5e 3f 7e 7e 5e 7e fe 9*7e 5e 3f 7e 7e 5e 7e fe 9*7e 5e 3f 5e 7f 7e 7c 7e fe
  //   8*7e 5e 3f 5e 7f 7e 7c 7e fe 8*7e 5e 3f 7e 7e fe 11*7e 5e 3f 7e 7e fe 11*7e 5e 3f fe 13*7e 5e 3f fe
  //   13*7e 5e 3f 5e 7f 5e 77 5e 7e 7c 7e fe 5*7e 5e 3f 5e 7f 5e 77 5e 7e 7c 7e fe 5*7e 5e 3f 5e 7f 5e 77
  //   5e 7e 7c 7e fe 5*7e 5e 3f 5e 7f 5e 77 5e 7e 7c 7e fe 5*7e 5e 3f 5e 7f 5e 77 5e 7e 7e fe 6*7e 5e 3f
  //   5e 7f 5e 77 5e 7e 7e fe 6*7e 5e 3f fe 13*7e 5e 3f fe 13*7e 5e 3f 5e 7f fe 11*7e 5e 3f 5e 7f 7c 7e 7e
  //   7c 7e fe 6*7e 5e 3f 5e 5f 76 5e 7a 7c 76 5e 7a 76 7e 7c 7e fe 5e 3f 5e 5f 76 5e 7a 7c 76 5e 7a 76 7e
  //   7c 7e fe 5e 3f fe 13*7e 5e 3f fe 13*7e 5e 3f fe 13*7e 5e 3f fe 13*7e 5e 3f fe 13*7e 5e 3f fe 13*7e
  //   5e 3f 5e 7f 7c 5e 7e 7c 7e fe 6*7e 5e 3f 5e 7f 7c 5e 7e 7c 7e fe 6*7e 5e 3f 5e 7f 7c 5e 7e 7e fe
  //   7*7e 5e 3f 5e 7f 7c 5e 7e 7e fe 7*7e 5e 3f fe 13*7e 5e 3f fe 13*7e 5e 3f 7e fe 12*7e 5e 3f 7e fe
  //   12*7e 5e 3f 5e 7f 7c 5e 77 5e 7a 76 7e 7c 7e fe 7e 7e 5e 3f 5e 7f 7c 5e 77 5e 7a 76 7e 7c 7e fe 7e
  //   7e 5e 3f fe 13*7e 5e 3f fe 13*7e 5e 3f fe 13*7e 5e 3f fe 13*7e 5e 3f fe 13*7e 5e 3f fe 13*7e 5e 3f
  //   5e 7f 7c 5e 77 5e 7a 76 7e 7c 7e fe 7e 7e 5e 3f 5e 7f 7c 5e 77 5e 7a 76 7e 7c 7e fe 7e 7e 5e 3f 5e
  //   7f 7c 5e 77 5e 7a 76 7e 7e fe 7e 7e 7e 5e 3f 5e 7f 7c 5e 77 5e 7a 76 7e 7e fe 7e 7e 7e 5e 3f fe
  //   13*7e 5e 3f fe 13*7e 5e 3f 7e 7e 5e 7e 7e 7e 5e 7e 7e 7e 5e 7e fe 7e 5e 3f 7e 7e 5e 7e 7e 7e 5e 7e
  //   7e 7e 5e 7e fe 7e 5e 3f 5e 7f 7c 5e 76 5e 7a 7c 76 5e 7e 7c 7e fe 5e 3f 5e 7f 7c 5e 76 5e 7a 7c 76
  //   5e 7e 7c 7e fe 5e 3f fe 13*7e 5e 3f fe 13*7e 5e 3f fe 13*7e 5e 3f fe 13*7e 5e 3f fe 13*7e 5e 3f fe
  //   13*7e 5e 3f 5e 5f 7e 7c 7e fe 8*7e 5e 3f 5e 5f 7e 7c 7e fe 8*7e 5e 3f 5e 5f 7e 7e fe 9*7e 5e 3f 5e
  //   5f 7e 7e fe 9*7e 5e 3f fe 13*7e 5e 3f fe 13*7e 5e 3f 5e 7e 7e fe 10*7e 5e 3f 5e 7e 7e fe 10*7e 5e 3f
  //   5e 7f 7e 7c 7e fe 8*7e 5e 3f 5e 7f 7e 7c 7e fe 8*7e 5e 3f 7e 7e fe 11*7e 5e 3f 7e 7e fe 11*7e 5e 3f
  //   fe 13*7e 5e 3f fe 13*7e 5e 3f 5e 7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
  //   contents of rom_4 (hex, n*v repeats v):
  //   1 c 6 1c c 6 c c 6 c c 5 c 5 4c c 1 c 6 1c c 6 c c 6 c c 5 c 5 4c c 1 c 1 1c c 5 14 c c 5 4 d c c 2c
  //   c 1 c 1 1c c 5 14 c c 5 4 d c c 2c c 1 15*c 1 15*c 1 15*c 1 15*c 1 15*c 1 15*c 1 c 1 5 c c 2c 9*c 1
  //   c 1 5 c c 2c 9*c 1 c 1 5 1e 3c 10*c 1 c 1 5 1e 3c 10*c 1 15*c 1 15*c 1 c 6 1c 12*c 1 c 6 1c 12*c 1 c
  //   0 d c c 2c 9*c 1 c 0 d c c 2c 9*c 1 c 1c 3c 12*c 1 c 1c 3c 12*c 1 15*c 1 15*c 1 15*c 1 15*c 1 c 1 c
  //   1 4 d c c 2c 6*c 1 c 1 c 1 4 d c c 2c 6*c 1 c 1 c 1 4 d 1e 3c 7*c 1 c 1 c 1 4 d 1e 3c 7*c 1 15*c 1
  //   15*c 1 c 1 c 1c 1c 10*c 1 c 1 13*c 1 c 1 5 14 c c 5 14 1c c 5 c c 2c c 1 c 1 5 14 c c 5 14 1c c 5 c
  //   c 2c c 1 15*c 1 15*c 1 15*c 1 15*c 1 15*c 1 15*c 1 c 1 1c c 5 c c 2c 7*c 1 c 1 1c c 5 c c 2c 7*c 1 c
  //   1 1c c 5 1e 3c 8*c 1 c 1 1c c 5 1e 3c 8*c 1 15*c 1 15*c 1 c 1c 13*c 1 c 1c 13*c 1 c 1 1c c 1 4 1c c
  //   5 c c 2c c c c 1 c 1 1c c 1 4 1c c 5 c c 2c c c c 1 15*c 1 15*c 1 15*c 1 15*c 1 15*c 1 15*c 1 c 1 1c
  //   c 1 4 1c c 5 c c 2c c c c 1 c 1 1c c 1 4 1c c 5 c c 2c c c c 1 c 1 1c c 1 4 1c c 5 1e 3c 4*c 1 c 1
  //   1c c 1 4 1c c 5 1e 3c 4*c 1 15*c 1 15*c 1 c 1 c 6 1c c 6 c c c 1 4*c 1 c 1 c 6 1c c 6 c c c 1 4*c 1
  //   c 1 1c c 5 14 c c 5 4 d c c 2c c 1 c 1 1c c 5 14 c c 5 4 d c c 2c c 1 15*c 1 15*c 1 15*c 1 15*c 1 c
  //   1 5 c c ac 9*c 1 c 1 5 c c ac 9*c 1 c 1 5 c c 2c 9*c 1 c 1 5 c c 2c 9*c 1 c 1 5 e 3c 10*c 1 c 1 5 e
  //   3c 10*c 1 15*c 1 15*c 1 c 1c c 5 11*c 1 c 1c c 5 11*c 1 c 0 d c c 2c 9*c 1 c 0 d c c 2c 9*c 1 c c 3c
  //   12*c 1 c c 3c 12*c 1 15*c 1 15*c 1 c 1 c 1 4 d c c ac 6*c 1 c 1 c 1 4 d c c ac 6*c 1 c 1 c 1 4 d c c
  //   2c 6*c 1 c 1 c 1 4 d c c 2c 6*c 1 c 1 c 1 4 d e 3c 7*c 1 c 1 c 1 4 d e 3c 7*c 1 15*c 1 15*c 1 c 1
  //   13*c 1 c 1 c 1c 1c 10*c 1 c 1 5 14 c c 5 14 1c c 5 c c 2c c 1 c 1 5 14 c c 5 14 1c c 5 c c 2c c 1
  //   15*c 1 15*c 1 15*c 1 15*c 1 15*c 1 15*c 1 c 1 1c c 5 c c 2c 7*c 1 c 1 1c c 5 c c 2c 7*c 1 c 1 1c c 5
  //   e 3c 8*c 1 c 1 1c c 5 e 3c 8*c 1 15*c 1 15*c 1 c 1c 13*c 1 c 1c 13*c 1 c 1 1c c 1 4 1c c 5 c c 2c c
  //   c c 1 c 1 1c c 1 4 1c c 5 c c 2c c c c 1 15*c 1 15*c 1 15*c 1 15*c 1 15*c 1 15*c 1 c 1 1c c 1 4 1c c
  //   5 c c 2c c c c 1 c 1 1c c 1 4 1c c 5 c c 2c c c c 1 c 1 1c c 1 4 1c c 5 e 3c 4*c 1 c 1 1c c 1 4 1c c
  //   5 e 3c 4*c 1 15*c 1 15*c 1 c 1c c 5 c 1c c 5 c 1c c 5 c c c 1 c 1c c 5 c 1c c 5 c 1c c 5 c c c 1 c 1
  //   1c c 5 14 c c 5 4 d c c 2c c 1 c 1 1c c 5 14 c c 5 4 d c c 2c c 1 15*c 1 15*c 1 15*c 1 15*c 1 15*c 1
  //   15*c 1 c 1 5 c c 2c 9*c 1 c 1 5 c c 2c 9*c 1 c 1 5 1e 3c 10*c 1 c 1 5 1e 3c 10*c 1 15*c 1 15*c 1 c 6
  //   1c 12*c 1 c 6 1c 12*c 1 c 0 d c c 2c 9*c 1 c 0 d c c 2c 9*c 1 c 1c 3c 12*c 1 c 1c 3c 12*c 1 15*c 1
  //   15*c 1 c 1 c 1 11*c 1 c 1 c 1 11*c 1 c 1 c 1 4 d c c 2c 6*c 1 c 1 c 1 4 d c c 2c 6*c 1 c 1 c 1 4 d
  //   1e 3c 7*c 1 c 1 c 1 4 d 1e 3c 7*c 1 15*c 1 15*c 1 c 81 c 1c 1c 10*c 1 c 81 13*c 1 c 1 5 14 c c 5 14
  //   1c c 5 c c 2c c 1 c 1 5 14 c c 5 14 1c c 5 c c 2c c 1 15*c 1 15*c 1 15*c 1 15*c 1 15*c 1 15*c 1 c 1
  //   1c c 5 c c 2c 7*c 1 c 1 1c c 5 c c 2c 7*c 1 c 1 1c c 5 1e 3c 8*c 1 c 1 1c c 5 1e 3c 8*c 1 15*c 1
  //   15*c 1 c 4c 13*c 1 c 4c 13*c 1 c 1 1c c 1 4 1c c 5 c c 2c c c c 1 c 1 1c c 1 4 1c c 5 c c 2c c c c 1
  //   15*c 1 15*c 1 15*c 1 15*c 1 15*c 1 15*c 1 c 1 1c c 1 4 1c c 5 c c 2c c c c 1 c 1 1c c 1 4 1c c 5 c c
  //   2c c c c 1 c 1 1c c 1 4 1c c 5 1e 3c 4*c 1 c 1 1c c 1 4 1c c 5 1e 3c 4*c 1 15*c 1 15*c 1 c 1c c 5 c
  //   c c 5 7*c 1 c 1c c 5 c c c 5 7*c 1 c 1 1c c 5 14 c c 5 4 d c c bc c 1 c 1 1c c 5 14 c c 5 4 d c c bc
  //   c 1 15*c 1 15*c 1 15*c 1 15*c 1 15*c 1 15*c 1 c 1 5 c c bc 9*c 1 c 1 5 c c bc 9*c 1 c 1 5 e 3c 10*c
  //   1 c 1 5 e 3c 10*c 1 15*c 1 15*c 1 c 1c c 5 c 2c 9*c 1 c 1c c 5 c 2c 9*c 1 c 0 d c c bc 9*c 1 c 0 d c
  //   c bc 9*c 1 c c 3c 12*c 1 c c 3c 12*c 1 15*c 1 15*c 1 c 1 c 1 4 d c 1c 1c c 5 4*c 1 c 1 c 1 4 d c 1c
  //   1c c 5 4*c 1 c 1 c 1 4 d c c bc 6*c 1 c 1 c 1 4 d c c bc 6*c 1 c 1 c 1 4 d e 3c 7*c 1 c 1 c 1 4 d e
  //   3c 7*c 1 15*c 1 15*c 1 c 81 13*c 1 c 81 c 1c 1c 10*c 1 c 1 5 14 c c 5 14 1c c 5 c c bc c 1 c 1 5 14
  //   c c 5 14 1c c 5 c c bc c 1 15*c 1 15*c 1 15*c 1 15*c 1 15*c 1 15*c 1 c 1 1c c 5 c c bc 7*c 1 c 1 1c
  //   c 5 c c bc 7*c 1 c 1 1c c 5 e 3c 8*c 1 c 1 1c c 5 e 3c 8*c 1 15*c 1 15*c 1 c 4c 13*c 1 c 4c 13*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
  //   contents of rom_5 (hex, n*v repeats v):
  //   c0 c0 88 c2 40 88 c0 40 88 c0 40 f0 c0 f8 c6 c0 c0 c0 88 c2 40 88 c0 40 88 c0 40 f0 c0 f8 c6 4*c0 82
  //   c0 0 c6 40 80 c0 c0 40 80 c0 41 4*c0 82 c0 0 c6 40 80 c0 c0 40 80 c0 41 101*c0 80 c0 41 13*c0 80 c0
  //   41 13*c0 82 41 14*c0 82 41 44*c0 88 c2 40 13*c0 88 c2 40 15*c0 80 c0 41 13*c0 80 c0 41 11*c0 82 41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
  //   contents of rom_6 (hex, n*v repeats v):
  //   2 2 7*6 4 6 7*2 7*6 4 6 7*2 10*6 2 2 3 2 2 2 10*6 2 2 3 103*2 3 15*2 3 14*2 3 15*2 3 44*2 6 4 6 13*2
  //   6 4 6 17*2 3 15*2 3 12*2 3 15*2 3 85*2 3 15*2 3 14*2 3 15*2 3 42*2 6 6 7 6 6 6 25*2 7*6 7 6 6 2 2 3
  //   2 2 2 7*6 7 6 6 2 2 3 99*2 4*6 2 2 3 9*2 4*6 2 2 3 9*2 4*6 2 3 10*2 4*6 2 3 74*2 5*6 7 6 6 2 2 3 5*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
  //   CARRY
  //   INSTRUCTION REGISTER
  //   MICROCODE TIMING
  //   ALU A INPUT
  //   ALU B INPUT
  //   N V H - d  I Z C 
  //   CONSTANT GENERATOR
  //   H will always show high here
  //   DATA BUS
  //   N V - - -   I Z C
  //   THIS IS USED TO SET PC TO $400 FOR KLAUS'S TEST
  //   PROGRAM COUNTER HIGH
  //   PROGRAM COUNTER LOW
  //   NOTE: MANUAL CONTROL WON'T WORK ANY MORE DUE TO INVERTED CONTROL SIGNALS
  //   STACK POINTER
  //   REGISTER X
  //   REGISTER Y
  //   ACCUMULATOR
  //   ADDRESS HIGH
  //   ADDRESS LOW
  //   FIXED ADDRESES H
  //   MICROCODED 6502-like CPU JuanGg on JANUARY 2019
  //   THIS IS FAR FROM FINISHED AND NO WARRANTIES ARE PROVIDED
  //   LICENSED UNDER GNU 3.0
  //   ADDED LACTHES FOR PROPPER BUS TIMING. KEYBOARD AND TERMINAL NO LONGER WORK
  //   AUX ADDRESS BUS
  //   READY
  //   PHI1
  //   PHI2
  //   RESET
  //   PHI1
  //   TESTS:
  //   A->B
  //   _CE
  //   R_W
  //   MICROCODE TIMING
  //   NMI
  //    64K RANDOM ACCESS MEMORY
endmodule

module _4_BIT_ALU_LOW (
  input  A0,
  input  A1,
  input  A2,
  input  A3,
  input  B0,
  input  B1,
  input  B2,
  input  B3,
  input  C_IN,
  input  S0,
  input  S1,
  input  S2,
  input  S3,
  output Y0,
  output Y1,
  output Y2,
  output Y3,
  output C_OUT,
  output ZERO,
  output OVF,
  output ROT
);

  ROM #(.addrWidth(13)) rom_1 (
    .addr({S3, S2, S1, S0, C_IN, B3, B2, B1, B0, A3, A2, A1, A0}),
    .data({ROT, OVF, ZERO, C_OUT, Y3, Y2, Y1, Y0}), .sel(1'b1));

  // Notes on the sheet:
  //   A
  //   B
  //   CTRL
  //   4-BIT ALU
  //   contents of rom_1 (hex, n*v repeats v):
  //   20 1 2 3 4 5 6 7 8 9 a b c d e f 20 1 2 3 4 5 6 7 8 9 a b c d e f 20 1 2 3 4 5 6 7 8 9 a b c d e f
  //   20 1 2 3 4 5 6 7 8 9 a b c d e f 20 1 2 3 4 5 6 7 8 9 a b c d e f 20 1 2 3 4 5 6 7 8 9 a b c d e f
  //   20 1 2 3 4 5 6 7 8 9 a b c d e f 20 1 2 3 4 5 6 7 8 9 a b c d e f 20 1 2 3 4 5 6 7 8 9 a b c d e f
  //   20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
  //   Y
endmodule

module _8_BIT_ALU (
  input  [7:0] A_INPUT,
  input  [7:0] B_INPUT,
  input  C_IN,
  input  [3:0] OP,
  output [7:0] OUT,
  output C_OUT,
  output ZERO,
  output OVF,
  output NEG
);

  wire dip_74157_1_p4, dip_74157_1_p7, n4_bit_alu_high_1_c_out, n4_bit_alu_high_1_zero,
       n4_bit_alu_low_1_c_out, n4_bit_alu_low_1_rot, n4_bit_alu_low_1_zero;

  _4_BIT_ALU_HIGH u_4_bit_alu_high_1 (
    .A0(A_INPUT[4]), .A1(A_INPUT[5]), .A2(A_INPUT[6]), .A3(A_INPUT[7]), .B0(B_INPUT[4]), .B1(B_INPUT[5]),
    .B2(B_INPUT[6]), .B3(B_INPUT[7]), .C_IN(dip_74157_1_p7), .S0(OP[0]), .S1(OP[1]), .S2(OP[2]), .S3(OP[3]),
    .Y0(OUT[4]), .Y1(OUT[5]), .Y2(OUT[6]), .Y3(NEG), .C_OUT(n4_bit_alu_high_1_c_out),
    .ZERO(n4_bit_alu_high_1_zero), .OVF(OVF));  // open: ROT
  _4_BIT_ALU_LOW u_4_bit_alu_low_1 (
    .A0(A_INPUT[0]), .A1(A_INPUT[1]), .A2(A_INPUT[2]), .A3(A_INPUT[3]), .B0(B_INPUT[0]), .B1(B_INPUT[1]),
    .B2(B_INPUT[2]), .B3(B_INPUT[3]), .C_IN(dip_74157_1_p4), .S0(OP[0]), .S1(OP[1]), .S2(OP[2]), .S3(OP[3]),
    .Y0(OUT[0]), .Y1(OUT[1]), .Y2(OUT[2]), .Y3(OUT[3]), .C_OUT(n4_bit_alu_low_1_c_out),
    .ZERO(n4_bit_alu_low_1_zero), .ROT(n4_bit_alu_low_1_rot));  // open: OVF
  // DIP_74157 dip_74157_1: pin names not known; wires that end beside it: n4_bit_alu_low_1_rot, C_IN, n4_bit_alu_high_1_c_out, dip_74157_1_p4, n4_bit_alu_low_1_c_out, C_IN, dip_74157_1_p7, 1'b0, 1'b0, 1'b0, n4_bit_alu_high_1_c_out, n4_bit_alu_low_1_c_out, C_OUT, OUT[3:0], {NEG, OUT[6:4]}
  Pull_Resistor pull_resistor_1 (.node(n4_bit_alu_low_1_rot));
  and and_1 (ZERO, n4_bit_alu_high_1_zero, n4_bit_alu_low_1_zero);

  assign OUT[7] = NEG;

  // Notes on the sheet:
  //    0 NOP, 1 NOT, 2 OR, 3 XOR, 4 AND, 5 ROL, 6 ROR, 7 SUM0, 8 SUB0, 9 SUM, 10 SUB, 11 SE, 12 BIT
  //   2 to 1 selector. Moves carry bits around for rotate right and shift right
  //   HIGH
  //   LOW
endmodule

module PC (
  input  [7:0] DATA_IN,
  input  CLK,
  input  CLEAR,
  input  LOAD,
  input  COUNT,
  output C_OUT,
  output [7:0] DATA_OUT
);

  wire dip_74161_2_p1, not_1_out, not_2_out;

  not not_1 (not_1_out, CLK);
  not not_2 (not_2_out, CLEAR);
  // DIP_74161 dip_74161_1: pin names not known; wires that end beside it: not_2_out, not_1_out, C_OUT
  // DIP_74161 dip_74161_2: pin names not known; wires that end beside it: dip_74161_2_p1, not_2_out, not_1_out, COUNT, dip_74161_2_p1, LOAD, dip_74161_2_p1, COUNT, LOAD
endmodule

module STATUS_REG (
  input  C,
  input  Z,
  input  V,
  input  N,
  input  C_C,
  input  C_Z,
  input  C_I,
  input  C_V,
  input  C_N,
  input  FGS,
  input  FGV,
  input  SRW,
  input  [7:0] BUS_IN,
  input  CLK,
  input  in_15,
  output [7:0] out_16,
  output CARRY,
  output I_DISABLE,
  output FLAG,
  output [7:0] BUS_OUT
);

  wire and_6_out, and_7_out, and_8_out, and_9_out, and_10_out, and_11_out, and_12_out, and_13_out,
       and_14_out, and_15_out, and_16_out, CLC, not_1_out, not_2_out, not_3_out, not_4_out, not_5_out,
       not_6_out, or_1_out, or_2_out, or_3_out, or_4_out, or_10_out, or_11_out, or_14_out, SEC, SEH, SEI,
       SEN, SEV, SEZ, SRWB;
  wire [3:0] multiplexer_2_out;
  wire [3:3] multiplexer_1_out;
  wire [7:0] multiplexer_3_out, or_6_out;

  Multiplexer #(.width(4)) multiplexer_1 (
    .in0({1'b0, BUS_OUT[0], SEH, C_C}), .in1({1'b0, out_16[5], 2'b00}),
    .out({multiplexer_1_out[3], CARRY, SEC, CLC}), .sel(in_15), .en(1'b1));
  Multiplexer #(.width(4)) multiplexer_2 (
    .in0({1'b0, V, Z, C}), .in1({4{FGV}}), .out(multiplexer_2_out), .sel(FGS), .en(1'b1));
  and and_1 (SEH, multiplexer_2_out[0], C_C);
  and and_2 (SEZ, multiplexer_2_out[1], C_Z);
  and and_3 (SEI, FGV, C_I);
  and and_4 (SEV, multiplexer_2_out[2], C_V);
  and and_5 (SEN, N, C_N);
  Multiplexer #(.width(8)) multiplexer_3 (
    .in0(BUS_IN), .in1({or_6_out[7:5], 2'b00, or_6_out[2:0]}), .out(multiplexer_3_out), .sel(SRWB), .en(1'b1));
  or or_1 (or_1_out, SRW, FGS);
  Register register_1 (
    .D(multiplexer_3_out), .en(or_1_out), .Q({BUS_OUT[7:6], out_16[5:4], BUS_OUT[3:0]}), .clk(CLK), .clr(1'b0));
  and and_6 (and_6_out, C_C, BUS_OUT[0]);
  or or_2 (or_2_out, C_C, C_Z);
  or or_3 (or_3_out, C_I, C_V);
  and and_7 (and_7_out, C_Z, BUS_OUT[1]);
  and and_8 (and_8_out, C_I, BUS_OUT[2]);
  or or_4 (or_4_out, or_2_out, or_3_out);
  or or_5 (SRWB, or_4_out, C_N);
  and and_9 (and_9_out, BUS_OUT[0], not_1_out);
  not not_1 (not_1_out, CLC);
  not not_2 (not_2_out, C_Z);
  and and_10 (and_10_out, C_V, BUS_OUT[6]);
  or or_6 (or_6_out[0], and_9_out, SEC);
  and and_11 (and_11_out, BUS_OUT[1], not_2_out);
  or or_7 (or_6_out[1], and_11_out, SEZ);
  not not_3 (not_3_out, C_I);
  not not_4 (not_4_out, C_C);
  and and_12 (and_12_out, C_N, BUS_OUT[7]);
  and and_13 (and_13_out, BUS_OUT[2], not_3_out);
  or or_8 (or_6_out[2], and_13_out, SEI);
  and and_14 (and_14_out, out_16[5], not_4_out);
  or or_9 (or_6_out[5], and_14_out, SEH);
  and and_15 (and_15_out, BUS_OUT[6], not_5_out);
  not not_5 (not_5_out, C_V);
  not not_6 (not_6_out, C_N);
  or or_10 (or_10_out, and_6_out, and_7_out);
  or or_11 (or_11_out, and_8_out, and_10_out);
  or or_12 (or_6_out[6], and_15_out, SEV);
  and and_16 (and_16_out, BUS_OUT[7], not_6_out);
  or or_13 (or_6_out[7], and_16_out, SEN);
  or or_14 (or_14_out, or_10_out, or_11_out);
  or or_15 (FLAG, or_14_out, and_12_out);

  assign BUS_OUT[5:4] = 2'b11;
  assign I_DISABLE = BUS_OUT[2];
  assign {out_16[7:6], out_16[3:0]} = {BUS_OUT[7:6], BUS_OUT[3:0]};

  // Other names for the same wires on the sheet: CLH = C_C; C_OUT = CARRY; C_t = BUS_OUT[0]; CLI = C_I; CLN = C_N;
  //   CLV = C_V; CLZ = C_Z; HCE = in_15; HC = out_16[5]

  // Notes on the sheet:
  //   PROCESSOR STATUS REGISTER
  //   SELECT REGULAR OR HIDDEN CARRY 
  //   SET SELECTED FLAGS
  //   FLAG VALUE FOR SELECTED FLAGS
  //   WRITE TO REGISTER, SELECTED FLAGS FROM ALU OR FROM THE BUS IF NONE
  //   HIDDEN CARRY ENABLE, USES THE HIDDEN CARRY FLAG FOR ADDRESS CALCULATIONS IN ORDER NOT TO MODIFY REGULAR CARRY. WE DONT CARE WHAT HAPPENS TO HC ON REGUALR OPERATION, IT GETS SET AND RESET WITH REGUALR CARRY.
  //   N V - - -  I  Z C
  //   HIDDEN CARRY
  //   IT DOES NOT PASS THE TEST IF UNUSED FLAGS ARE NOT 1
endmodule

module _4_BIT_ALU_HIGH (
  input  A0,
  input  A1,
  input  A2,
  input  A3,
  input  B0,
  input  B1,
  input  B2,
  input  B3,
  input  C_IN,
  input  S0,
  input  S1,
  input  S2,
  input  S3,
  output Y0,
  output Y1,
  output Y2,
  output Y3,
  output C_OUT,
  output ZERO,
  output OVF,
  output ROT
);

  ROM #(.addrWidth(13)) rom_1 (
    .addr({S3, S2, S1, S0, C_IN, B3, B2, B1, B0, A3, A2, A1, A0}),
    .data({ROT, OVF, ZERO, C_OUT, Y3, Y2, Y1, Y0}), .sel(1'b1));

  // Notes on the sheet:
  //   A
  //   B
  //   CTRL
  //   4-BIT ALU
  //   contents of rom_1 (hex, n*v repeats v):
  //   20 1 2 3 4 5 6 7 8 9 a b c d e f 20 1 2 3 4 5 6 7 8 9 a b c d e f 20 1 2 3 4 5 6 7 8 9 a b c d e f
  //   20 1 2 3 4 5 6 7 8 9 a b c d e f 20 1 2 3 4 5 6 7 8 9 a b c d e f 20 1 2 3 4 5 6 7 8 9 a b c d e f
  //   20 1 2 3 4 5 6 7 8 9 a b c d e f 20 1 2 3 4 5 6 7 8 9 a b c d e f 20 1 2 3 4 5 6 7 8 9 a b c d e f
  //   20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
  //   Y
endmodule

module CONSTANT_GENERATOR (
  input  CG0,
  input  CG1,
  input  CG2,
  input  RST_INS,
  input  NMI_INS,
  output [7:0] HIGH,
  output [7:0] LOW
);

  wire or_1_out, or_3_out;
  wire [2:0] and_1_out;
  wire [7:0] or_5_out;

  or or_1 (or_1_out, CG0, RST_INS);
  or or_2 (and_1_out[1], CG1, RST_INS);
  or or_3 (or_3_out, CG2, RST_INS);
  or or_4 (and_1_out[2], or_3_out, NMI_INS);
  or or_5 (or_5_out[0], or_1_out, or_5_out[7]);
  or or_6 (or_5_out[7], and_1_out[1], and_1_out[2]);
  and and_1 (and_1_out[0], or_1_out, or_5_out[7]);
  assign HIGH = or_5_out[0] ? {{7{or_5_out[7]}}, or_5_out[0]} : 8'bz;  // Controlled_Buffer controlled_buffer_1
  assign LOW = or_5_out[7] ? {{5{or_5_out[7]}}, and_1_out} : 8'bz;  // Controlled_Buffer controlled_buffer_2

  // Notes on the sheet:
  //   000: RELEASE BUS, 001: SP, 010: NMI1, 011: NMI2, 100:R1, 101:R2, 110: IRQ1, 111: IRQ2
endmodule
